// Logisim project 4 Bit Aritmetik Mantık Birimi Tasarımı .circ as structural Verilog: 8 circuits, main circuit FullAdder
module main (
  input  [3:0] Operand_a,
  input  [3:0] Operand_b,
  input  [3:0] Opcode,
  input  LOAD_Btn,
  input  EXEC_Btn,
  input  RESET_Btn
);

  wire and_1_out, and_2_out, and_3_out, and_4_out, and_5_out, and_6_out, and_7_out, and_8_out, clock_1_out,
       d_ff_1_q, d_ff_1_qn, d_ff_2_q, d_ff_2_qn, logicunit_1_carry, logicunit_1_sign, logicunit_1_zero,
       not_1_out, not_2_out, or_1_out, or_2_out;
  wire [3:0] logicunit_1_out_7, register_1_q, register_2_q, register_3_q;

  Register #(.width(4)) register_1 (.D(Operand_a), .en(and_7_out), .clk(clock_1_out), .Q(register_1_q));  // open: clr
  Register #(.width(4)) register_2 (.D(Operand_b), .en(and_7_out), .clk(clock_1_out), .Q(register_2_q));  // open: clr
  not not_1 (not_1_out, RESET_Btn);
  and and_1 (and_1_out, EXEC_Btn, d_ff_2_q);
  or or_1 (or_1_out, and_1_out, d_ff_1_q);
  and and_2 (and_2_out, or_1_out, not_1_out);
  not not_2 (not_2_out, EXEC_Btn);
  Clock clock_1 (.out(clock_1_out));
  and and_3 (and_3_out, d_ff_1_qn, d_ff_2_qn, not_2_out);
  and and_4 (and_4_out, d_ff_1_qn, d_ff_2_q, LOAD_Btn);
  and and_5 (and_5_out, d_ff_1_q, RESET_Btn);
  D_Flip_Flop d_ff_1 (.D(and_2_out), .clk(clock_1_out), .Q(d_ff_1_q), .Qn(d_ff_1_qn));  // open: preset, reset
  D_Flip_Flop d_ff_2 (.D(and_6_out), .clk(clock_1_out), .Q(d_ff_2_q), .Qn(d_ff_2_qn));  // open: preset, reset
  and and_6 (and_6_out, or_2_out, not_1_out);
  or or_2 (or_2_out, and_3_out, and_4_out, and_5_out);
  and and_7 (and_7_out, d_ff_1_qn, d_ff_2_q);
  and and_8 (and_8_out, d_ff_1_q, d_ff_2_qn);
  LED led_1 (.in(logicunit_1_sign));
  LED led_2 (.in(logicunit_1_carry));
  LogicUnit logicunit_1 (
    .A(register_2_q), .B(register_1_q), .Opcode(Opcode), .Sign(logicunit_1_sign), .Carry(logicunit_1_carry),
    .Zero(logicunit_1_zero), .out_7(logicunit_1_out_7));
  Register #(.width(4)) register_3 (
    .D(logicunit_1_out_7), .en(and_8_out), .clk(clock_1_out), .Q(register_3_q), .clr(RESET_Btn));
  LED led_3 (.in(logicunit_1_zero));
  Hex_Digit_Display hex_digit_display_1 (.value(register_3_q));  // open: dp
endmodule

module FullAdder (
  input  A,
  input  B,
  input  Cin,
  output S,
  output Cout
);

  wire and_1_out, and_2_out, xor_1_out;

  xor xor_1 (xor_1_out, A, B);
  and and_1 (and_1_out, A, B);
  xor xor_2 (S, xor_1_out, Cin);
  and and_2 (and_2_out, xor_1_out, Cin);
  or or_1 (Cout, and_2_out, and_1_out);
endmodule

module Adder4 (
  input  [3:0] A,
  input  [3:0] B,
  input  Carry_in,
  output [3:0] Result,
  output Carry
);

  wire fulladder_1_cout, fulladder_2_cout, fulladder_3_cout;

  FullAdder fulladder_1 (.A(A[0]), .B(B[0]), .Cin(Carry_in), .S(Result[0]), .Cout(fulladder_1_cout));
  FullAdder fulladder_2 (.A(A[1]), .B(B[1]), .Cin(fulladder_1_cout), .S(Result[1]), .Cout(fulladder_2_cout));
  FullAdder fulladder_3 (.A(A[2]), .B(B[2]), .Cin(fulladder_2_cout), .S(Result[2]), .Cout(fulladder_3_cout));
  FullAdder fulladder_4 (.A(A[3]), .B(B[3]), .Cin(fulladder_3_cout), .S(Result[3]), .Cout(Carry));
endmodule

module Subtractor4 (
  input  [3:0] A,
  input  [3:0] B,
  output [3:0] Result,
  output Carry
);

  wire [3:0] not_1_out;

  assign not_1_out = ~B;  // NOT_Gate not_1, 4 bits wide
  Adder4 adder4_1 (.Result(Result), .A(A), .B(not_1_out), .Carry_in(1'b1), .Carry(Carry));
endmodule

module LogicUnit (
  input  [3:0] A,
  input  [3:0] B,
  input  [3:0] Opcode,
  output Carry,
  output Sign,
  output Zero,
  output [3:0] out_7
);

  wire adder4_1_carry, and_2_out, and_3_out, incrementer4_1_carry, not_2_out, not_3_out, not_4_out,
       not_5_out, or_2_out, subtractor4_1_carry;
  wire [3:0] adder4_1_result, and_1_out, decrementer4_1_result, divider4_1_out_3, incrementer4_1_result,
       not_1_out, or_1_out, subtractor4_1_result, xor_1_out;

  Adder4 adder4_1 (.Result(adder4_1_result), .A(B), .B(A), .Carry(adder4_1_carry));  // open: Carry_in
  Subtractor4 subtractor4_1 (.A(A), .B(B), .Result(subtractor4_1_result), .Carry(subtractor4_1_carry));
  Incrementer4 incrementer4_1 (.In(A), .Result(incrementer4_1_result), .Carry(incrementer4_1_carry));
  assign and_1_out = A & B;  // AND_Gate and_1, 4 bits wide
  assign or_1_out = A | B;  // OR_Gate or_1, 4 bits wide
  assign xor_1_out = A ^ B;  // XOR_Gate xor_1, 4 bits wide
  assign not_1_out = ~A;  // NOT_Gate not_1, 4 bits wide
  Decrementer4 decrementer4_1 (.In(A), .Result(decrementer4_1_result));
  Divider4 divider4_1 (.A(A), .B(B), .out_3(divider4_1_out_3));
  or or_2 (or_2_out, adder4_1_carry, incrementer4_1_carry);
  not not_2 (not_2_out, Opcode[0]);
  not not_3 (not_3_out, Opcode[1]);
  not not_4 (not_4_out, Opcode[2]);
  not not_5 (not_5_out, Opcode[3]);
  Multiplexer #(.enable("true"), .select(4), .width(4)) multiplexer_1 (
    .in0(adder4_1_result), .in1(subtractor4_1_result), .in2(incrementer4_1_result),
    .in3(decrementer4_1_result), .in4(divider4_1_out_3), .in5(and_1_out), .in6(or_1_out), .in7(xor_1_out),
    .in8(not_1_out), .out(out_7), .sel(Opcode), .en(1'b1));  // open: in9, in10, in11, in12, in13, in14, in15
  and and_2 (and_2_out, not_2_out, not_3_out, not_4_out, not_5_out, or_2_out);
  and and_3 (and_3_out, Opcode[0], not_2_out, not_4_out, not_5_out, subtractor4_1_carry);
  or or_3 (Carry, and_2_out, and_3_out);
  or or_4 (Zero, out_7[0], out_7[1], out_7[2], out_7[3]);

  assign Sign = out_7[3];
endmodule

module Incrementer4 (
  input  [3:0] In,
  output [3:0] Result,
  output Carry
);

  wire fulladder_1_cout, fulladder_2_cout, fulladder_3_cout;

  FullAdder fulladder_1 (.A(In[0]), .B(1'b1), .Cin(1'b0), .S(Result[0]), .Cout(fulladder_1_cout));
  FullAdder fulladder_2 (.A(In[1]), .B(1'b0), .Cin(fulladder_1_cout), .S(Result[1]), .Cout(fulladder_2_cout));
  FullAdder fulladder_3 (.A(In[2]), .B(1'b0), .Cin(fulladder_2_cout), .S(Result[2]), .Cout(fulladder_3_cout));
  FullAdder fulladder_4 (.A(In[3]), .B(1'b0), .Cin(fulladder_3_cout), .S(Result[3]), .Cout(Carry));
endmodule

module Divider4 (
  input  [3:0] A,
  input  [3:0] B,
  output [3:0] out_3
);

  wire subtractor4_1_carry;
  wire [3:0] not_1_out, subtractor4_1_result;

  Subtractor4 subtractor4_1 (.A({3'b000, A[3]}), .B(B), .Result(subtractor4_1_result), .Carry(subtractor4_1_carry));
  Multiplexer #(.width(4)) multiplexer_1 (.in0(4'b0000), .in1(not_1_out), .out(out_3), .sel(subtractor4_1_carry));
  assign not_1_out = ~subtractor4_1_result;  // NOT_Gate not_1, 4 bits wide
  // also tied to GND on the sheet: {A[0], A[1], A[2]}
endmodule

module Decrementer4 (
  input  [3:0] In,
  output [3:0] Result
);

  // Subtractor4 subtractor4_1: pin names not known; wires that end beside it: Result, In, 4'b0001
endmodule
